// Logisim project RRISC.circ as structural Verilog: 4 circuits, main circuit main
module main (
);

  wire ACC_OUT_IS_JUMP, ACC_OUT_IS_SKIP, and_2_out, and_3_out, and_4_out, CLK, comparator_1_eq,
       comparator_2_eq, EX, INST_RB, INST_WB, INSTF, MEM_WRITE, not_1_out, RST, WB, WRITEFLAG;
  wire [0:0] not_2_out;
  wire [3:0] ACC_OUT_RX_WB;
  wire [7:0] ALU_OUT_RESULT, IR_q, MEM_DATA, MEMDATAIN, multiplexer_3_out, R0_ACC, RCD, RCS, register_1_q,
       register_2_q;
  wire [15:0] adder_1_out, MEM_PC, MEMBUS, multiplexer_2_out, REGS_OUT_MEM;

  Multiplexer #(.enable("false"), .width(16)) multiplexer_1 (
    .in0(REGS_OUT_MEM), .in1(MEM_PC), .out(MEMBUS), .sel(INSTF));
  and and_1 (MEM_WRITE, INST_WB, WRITEFLAG);
  Comparator #(.width(16)) comparator_1 (.a(16'hf0f0), .b(MEMBUS), .eq(comparator_1_eq));  // open: gt, lt
  Comparator #(.width(16)) comparator_2 (.a(16'hf0f1), .b(MEMBUS), .eq(comparator_2_eq));  // open: gt, lt
  RAM #(.addrWidth(16), .clearpin("true"), .databus("bidir"), .trigger("high")) ram_1 (
    .addr(MEMBUS), .we(MEM_WRITE), .oe(not_1_out), .clk(not_1_out), .data(MEM_DATA), .clr(RST));
  not not_1 (not_1_out, MEM_WRITE);
  and and_2 (and_2_out, MEM_WRITE, comparator_1_eq);
  and and_3 (and_3_out, MEM_WRITE, comparator_2_eq);
  Register #(.width(16)) PC (.D(multiplexer_2_out), .en(1'b1), .clk(WB), .Q(MEM_PC), .clr(RST));
  Multiplexer #(.enable("false"), .width(16)) multiplexer_2 (
    .in0(adder_1_out), .in1(REGS_OUT_MEM), .out(multiplexer_2_out), .sel(ACC_OUT_IS_JUMP));
  not not_2 (not_2_out[0], ACC_OUT_IS_SKIP);
  Register register_1 (.D(MEM_DATA), .en(and_2_out), .clk(CLK), .Q(register_1_q), .clr(RST));
  Register register_2 (.D(MEM_DATA), .en(and_3_out), .clk(CLK), .Q(register_2_q), .clr(RST));
  Adder #(.width(16)) adder_1 (
    .a(MEM_PC), .b({{14{1'b0}}, ACC_OUT_IS_SKIP, not_2_out[0]}), .out(adder_1_out));  // open: cin, cout
  assign MEM_DATA = MEM_WRITE ? MEMDATAIN : 8'bz;  // Controlled_Buffer controlled_buffer_1
  _7_Segment_Display u_7_segment_display_1 (
    .g(register_1_q[6]), .f(register_1_q[5]), .a(register_1_q[0]), .b(register_1_q[1]), .e(register_1_q[4]),
    .d(register_1_q[3]), .c(register_1_q[2]), .dp(register_1_q[7]));
  _7_Segment_Display u_7_segment_display_2 (
    .g(register_2_q[6]), .f(register_2_q[5]), .a(register_2_q[0]), .b(register_2_q[1]), .e(register_2_q[4]),
    .d(register_2_q[3]), .c(register_2_q[2]), .dp(register_2_q[7]));
  Register IR (.D(MEM_DATA), .en(1'b1), .clk(EX), .Q(IR_q), .clr(RST));
  // Probe on MEM_DATA
  Button BRST (.out(RST));
  // Probe on IR_q
  and and_4 (and_4_out, WRITEFLAG, ~INST_WB);  // AND_Gate
  // Probe on multiplexer_3_out
  Multiplexer #(.enable("false"), .width(8)) multiplexer_3 (
    .in0(ALU_OUT_RESULT), .in1(MEM_DATA), .out(multiplexer_3_out), .sel(INST_RB));
  // Probe on ACC_OUT_RX_WB
  Controller controller_1 (.RST(RST), .INSTF(INSTF), .EX(EX), .WB(WB), .OUT_CLK(CLK));
  D_Flip_Flop #(.trigger("falling")) d_ff_1 (.D(EX), .clk(CLK), .Q(WRITEFLAG), .reset(RST));  // open: Qn, preset
  and u_INST_RB (INST_RB, ~IR_q[4], IR_q[5], IR_q[6], IR_q[7]);  // AND_Gate
  and u_INST_WB (INST_WB, IR_q[4], IR_q[5], IR_q[6], IR_q[7]);
  // Probe on R0_ACC
  REGS regs_1 (
    .RST(RST), .Data(multiplexer_3_out), .CLK(WB), .Write(and_4_out), .Rx_Read(IR_q[3:0]),
    .Rx_Write(ACC_OUT_RX_WB), .OUT_R0_ACC(R0_ACC), .OUT_REGDATA(MEMDATAIN), .OUT_RCS(RCS), .OUT_RCD(RCD),
    .OUT_MEM(REGS_OUT_MEM));
  // Probe on ALU_OUT_RESULT
  ALU alu_1 (
    .IN_ACC(R0_ACC), .IN_RCS(RCS), .IN_RCD(RCD), .OPCODE(IR_q[7:4]), .IN_IMMEDIATE(IR_q[3:0]),
    .REGDATA(MEMDATAIN), .IN_WB_FLAGS(WB), .IN_RST_FLAGS(RST), .OUT_RESULT(ALU_OUT_RESULT),
    .OUT_RX_WB(ACC_OUT_RX_WB), .OUT_IS_JUMP(ACC_OUT_IS_JUMP), .OUT_IS_SKIP(ACC_OUT_IS_SKIP));
  // Probe on R0_ACC
  // Probe on MEMDATAIN
  // Probe on RCS
  // Probe on RCD
  // Probe on REGS_OUT_MEM
  // Probe on ALU_OUT_RESULT

  // Other names for the same wires on the sheet: MEMDATAOUT[7:0] = MEM_DATA

  // Notes on the sheet:
  //   An Example of Memory-Mapped IO
  //   An Example of Memory-Mapped IO
  //   40MHz = 25ns
  //   30MHz = 33.3ns
  //   20MHz = 50ns
  //   15MHz = 66.6ns
  //   10MHz = 100ns
  //   11ns
  //   <- Expected 16MHz
  //   <- Test around 1kHz
  //   TODO consider Harvard VS Von-Neumann
  //   34ns - 74xx283
  //   Has RST no WE, such as 74xx 273
  //   6ns
  //   TODO is this necessary?
  //   Put in ALU?
  //   Has RST no WE
  //   Every stage MUST effect state logic
  //   5ns 74as
  //   ~40ns
  //   12ns
  //   34:14
  //   Instf: Sets mem to PC. Data clocked into IR at end.
  //   EX: Spends cycle feeding-through ALU. Data clocked into WB at end.
  //   WE Pulled high for cycle. Writes to registers. Writes to memory if inst_memwrite
  //   Hardware:
  //   ~20 Registers
  //   1 64k SRAM
  //   ~50 logic gates
  //   ~20 ALU logic gates
  //   ~10 PC Board
  //   ~10 regfile logic gates
  //   ~6 MB logic gates
  //   ~5 MMIO SRAM
endmodule

module ALU (
  input  [7:0] IN_ACC,
  input  [7:0] IN_RCS,
  input  [7:0] IN_RCD,
  input  [3:0] OPCODE,
  input  [3:0] IN_IMMEDIATE,
  input  [7:0] REGDATA,
  input  IN_WB_FLAGS,
  input  IN_RST_FLAGS,
  output [7:0] OUT_RESULT,
  output [3:0] OUT_RX_WB,
  output OUT_IS_JUMP,
  output OUT_IS_SKIP
);

  wire and_1_out, and_2_out, and_4_out, comparator_1_eq, comparator_1_gt, comparator_1_lt, FLAG_CARRY_IN,
       FLAG_CARRY_OUT, multiplexer_4_out, nor_1_out, not_1_out, not_2_out, or_1_out, or_2_out, xor_1_out;
  wire [3:0] bit_extender_1_out;
  wire [7:0] adder_1_out, and_7_out, bit_extender_2_out, multiplexer_5_out, multiplexer_6_out,
       multiplexer_7_out, multiplexer_8_out, or_3_out, REG_OR_ONESIMM, xor_2_out, xor_3_out;
  wire [7:4] REG_OR_ZEROIMM;

  and and_1 (and_1_out, OPCODE[0], OPCODE[1], OPCODE[2]);
  and and_2 (and_2_out, OPCODE[1], OPCODE[2], OPCODE[3]);
  Comparator #(.mode("unsigned")) comparator_1 (
    .a(IN_RCS), .b(IN_RCD), .gt(comparator_1_gt), .eq(comparator_1_eq), .lt(comparator_1_lt));
  or or_1 (or_1_out, and_1_out, and_2_out);
  or or_2 (or_2_out, IN_RCS[0], IN_RCS[1], IN_RCS[2], IN_RCS[3], IN_RCS[4], IN_RCS[5], IN_RCS[6], IN_RCS[7]);
  assign bit_extender_1_out = {{3{or_1_out}}, or_1_out};  // Bit_Extender bit_extender_1
  Multiplexer #(.enable("false"), .width(4)) multiplexer_1 (
    .in0(4'b1111), .in1(REGDATA[7:4]), .out(REG_OR_ONESIMM[7:4]), .sel(OPCODE[0]));
  Multiplexer #(.enable("false"), .width(4)) multiplexer_2 (
    .in0(4'b0000), .in1(REGDATA[7:4]), .out(REG_OR_ZEROIMM), .sel(OPCODE[0]));
  Multiplexer #(.enable("false"), .width(4)) multiplexer_3 (
    .in0(IN_IMMEDIATE), .in1(REGDATA[3:0]), .out(REG_OR_ONESIMM[3:0]), .sel(OPCODE[0]));
  Multiplexer #(.enable("false"), .select(3)) multiplexer_4 (
    .in0(1'b1), .in1(or_2_out), .in2(IN_RCS[7]), .in3(comparator_1_lt), .in4(comparator_1_eq),
    .in5(comparator_1_gt), .in6(IN_RCS[0]), .in7(FLAG_CARRY_OUT), .out(multiplexer_4_out),
    .sel(IN_IMMEDIATE[3:1]));
  assign OUT_RX_WB = IN_IMMEDIATE & bit_extender_1_out;  // AND_Gate and_3, 4 bits wide
  xor xor_1 (xor_1_out, multiplexer_4_out, IN_IMMEDIATE[0]);
  not not_1 (not_1_out, OPCODE[1]);
  and and_4 (and_4_out, OPCODE[3], OPCODE[2], not_1_out, xor_1_out);
  assign bit_extender_2_out = {{7{OPCODE[1]}}, OPCODE[1]};  // Bit_Extender bit_extender_2
  not not_2 (not_2_out, OPCODE[0]);
  assign xor_2_out = bit_extender_2_out ^ {REG_OR_ZEROIMM, REG_OR_ONESIMM[3:0]};  // XOR_Gate xor_2, 8 bits wide
  and and_5 (OUT_IS_JUMP, and_4_out, OPCODE[0]);
  and and_6 (OUT_IS_SKIP, and_4_out, not_2_out);
  Adder adder_1 (.a(IN_ACC), .b(xor_2_out), .out(adder_1_out), .cin(OPCODE[1]), .cout(FLAG_CARRY_IN));
  assign and_7_out = IN_ACC & REG_OR_ONESIMM;  // AND_Gate and_7, 8 bits wide
  Multiplexer #(.enable("false"), .width(8)) multiplexer_5 (
    .in0(REGDATA), .in1(IN_ACC), .out(multiplexer_5_out), .sel(OPCODE[0]));
  assign or_3_out = IN_ACC | {REG_OR_ZEROIMM, REG_OR_ONESIMM[3:0]};  // OR_Gate or_3, 8 bits wide
  assign xor_3_out = IN_ACC ^ {REG_OR_ZEROIMM, REG_OR_ONESIMM[3:0]};  // XOR_Gate xor_3, 8 bits wide
  nor nor_1 (nor_1_out, OPCODE[3], OPCODE[2]);
  Register #(.width(1)) FLAG_CARRY (
    .D(FLAG_CARRY_IN), .en(nor_1_out), .clk(IN_WB_FLAGS), .Q(FLAG_CARRY_OUT), .clr(IN_RST_FLAGS));
  Multiplexer #(.enable("false"), .width(8)) multiplexer_6 (
    .in0({and_7_out[3:0], and_7_out[7:4]}), .in1(and_7_out), .out(multiplexer_6_out), .sel(OPCODE[0]));
  Multiplexer #(.enable("false"), .width(8)) multiplexer_7 (
    .in0({or_3_out[3:0], or_3_out[7:4]}), .in1(or_3_out), .out(multiplexer_7_out), .sel(OPCODE[0]));
  Multiplexer #(.enable("false"), .width(8)) multiplexer_8 (
    .in0({xor_3_out[3:0], xor_3_out[7:4]}), .in1(xor_3_out), .out(multiplexer_8_out), .sel(OPCODE[0]));
  Multiplexer #(.enable("false"), .select(3), .width(8)) multiplexer_9 (
    .in0(adder_1_out), .in1(adder_1_out), .in2(multiplexer_6_out), .in3(multiplexer_5_out),
    .in4(multiplexer_7_out), .in5(multiplexer_8_out), .in6(IN_ACC), .in7({8{1'b0}}), .out(OUT_RESULT),
    .sel(OPCODE[3:1]));

  // Other names for the same wires on the sheet: IMMEDIATE[3:0] = IN_IMMEDIATE; OPCODE_LSB = OPCODE[0];
  //   OPCODE_BIT1 = OPCODE[1]; REG_OR_ZEROIMM[3:0] = REG_OR_ONESIMM[3:0]

  // Notes on the sheet:
  //   If set, WB, or RB instruction: (DST=IMM) ELSE (DST=ACC)
  //   ROI [3:0]
  //   Data is register or immediate. The 4MSB of imm are 1s for AND and 0s for xor,add,or
  //   Conditional Jump
  //   Branch Event
  //   Consider putting this on a Program Counter daughter board
  //   Branch event and instruction
  //   ANDI/AND
  //   GET/SET
  //   ORI/OR
  //   XORI/XOR
  //   WE = add/sub = opcode 0-3
  //   ~40ns
  //   The actual ALU
  //   18.5ns
  //   ADDI/ADD/SUBI/SUB
  //   Has RST or WE
  //   SIF/JIF
  //   RB/WB
  //   11ns
  //   Actual ALU Stuff
  //   ~40ns
endmodule

module REGS (
  input  RST,
  input  [7:0] Data,
  input  CLK,
  input  Write,
  input  [3:0] Rx_Read,
  input  [3:0] Rx_Write,
  output [7:0] OUT_R0_ACC,
  output [7:0] OUT_REGDATA,
  output [7:0] OUT_RCS,
  output [7:0] OUT_RCD,
  output [15:0] OUT_MEM
);

  wire demultiplexer_1_out0, demultiplexer_1_out1, demultiplexer_1_out2, demultiplexer_1_out3,
       demultiplexer_1_out4, demultiplexer_1_out5, demultiplexer_1_out6, demultiplexer_1_out7,
       demultiplexer_1_out8, demultiplexer_1_out9, demultiplexer_1_out10, demultiplexer_1_out11,
       demultiplexer_1_out12, demultiplexer_1_out13, demultiplexer_1_out14, demultiplexer_1_out15;
  wire [7:0] R1_q, R2_q, R3_q, R4_q, R5_q, R6_q, R7_q, R8_q, R9_RAT_q, RA_RSH_q, RB_RSL_q;

  Demultiplexer #(.enable("false"), .select(4)) demultiplexer_1 (
    .out0(demultiplexer_1_out0), .out1(demultiplexer_1_out1), .out2(demultiplexer_1_out2),
    .out3(demultiplexer_1_out3), .out4(demultiplexer_1_out4), .out5(demultiplexer_1_out5),
    .out6(demultiplexer_1_out6), .out7(demultiplexer_1_out7), .out8(demultiplexer_1_out8),
    .out9(demultiplexer_1_out9), .out10(demultiplexer_1_out10), .out11(demultiplexer_1_out11),
    .out12(demultiplexer_1_out12), .out13(demultiplexer_1_out13), .out14(demultiplexer_1_out14),
    .out15(demultiplexer_1_out15), .in(Write), .sel(Rx_Write));
  Register R0_ACC (.D(Data), .en(demultiplexer_1_out0), .clk(CLK), .Q(OUT_R0_ACC), .clr(RST));
  Register R1 (.D(Data), .en(demultiplexer_1_out1), .clk(CLK), .Q(R1_q), .clr(RST));
  Register R2 (.D(Data), .en(demultiplexer_1_out2), .clk(CLK), .Q(R2_q), .clr(RST));
  Register R3 (.D(Data), .en(demultiplexer_1_out3), .clk(CLK), .Q(R3_q), .clr(RST));
  Register R4 (.D(Data), .en(demultiplexer_1_out4), .clk(CLK), .Q(R4_q), .clr(RST));
  Register R5 (.D(Data), .en(demultiplexer_1_out5), .clk(CLK), .Q(R5_q), .clr(RST));
  Register R6 (.D(Data), .en(demultiplexer_1_out6), .clk(CLK), .Q(R6_q), .clr(RST));
  Register R7 (.D(Data), .en(demultiplexer_1_out7), .clk(CLK), .Q(R7_q), .clr(RST));
  Register R8 (.D(Data), .en(demultiplexer_1_out8), .clk(CLK), .Q(R8_q), .clr(RST));
  Register R9_RAT (.D(Data), .en(demultiplexer_1_out9), .clk(CLK), .Q(R9_RAT_q), .clr(RST));
  Register RA_RSH (.D(Data), .en(demultiplexer_1_out10), .clk(CLK), .Q(RA_RSH_q), .clr(RST));
  Register RB_RSL (.D(Data), .en(demultiplexer_1_out11), .clk(CLK), .Q(RB_RSL_q), .clr(RST));
  Register RC_RCS (.D(Data), .en(demultiplexer_1_out12), .clk(CLK), .Q(OUT_RCS), .clr(RST));
  Register RD_RCD (.D(Data), .en(demultiplexer_1_out13), .clk(CLK), .Q(OUT_RCD), .clr(RST));
  Register RE_RMH (.D(Data), .en(demultiplexer_1_out14), .clk(CLK), .Q(OUT_MEM[15:8]), .clr(RST));
  Register RF_RML (.D(Data), .en(demultiplexer_1_out15), .clk(CLK), .Q(OUT_MEM[7:0]), .clr(RST));
  Multiplexer #(.enable("false"), .select(4), .width(8)) multiplexer_1 (
    .in0(OUT_R0_ACC), .in1(R1_q), .in2(R2_q), .in3(R3_q), .in4(R4_q), .in5(R5_q), .in6(R6_q), .in7(R7_q),
    .in8(R8_q), .in9(R9_RAT_q), .in10(RA_RSH_q), .in11(RB_RSL_q), .in12(OUT_RCS), .in13(OUT_RCD),
    .in14(OUT_MEM[15:8]), .in15(OUT_MEM[7:0]), .out(OUT_REGDATA), .sel(Rx_Read));

  // Notes on the sheet:
  //   6ns
  //   6ns
  //   Has WE no RST, such as 74xx 377
  //   Is actually 8 16:1 muxes
endmodule

module Controller (
  input  RST,
  output INSTF,
  output EX,
  output WB,
  output OUT_CLK
);

  D_Flip_Flop d_ff_1 (.D(WB), .clk(OUT_CLK), .Q(INSTF), .preset(RST));  // open: Qn, reset
  Clock clock_1 (.out(OUT_CLK));
  D_Flip_Flop d_ff_2 (.D(INSTF), .clk(OUT_CLK), .Q(EX), .reset(RST));  // open: Qn, preset
  D_Flip_Flop d_ff_3 (.D(EX), .clk(OUT_CLK), .Q(WB), .reset(RST));  // open: Qn, preset
endmodule
